// Digital circuit hardware.dig as structural Verilog
module hardware (
  input  clk,
  input  [3:0] in_2,
  input  [3:0] in_3,
  input  in_4,
  input  in_5,
  input  in_6,
  input  [15:0] in_7,
  input  in_8,
  input  in_9,
  input  [15:0] in_10
);

  wire control_1_p6, control_1_p7, InstrEx, InstrL, PC_ovf, RTW;
  wire [3:0] RT;
  wire [7:0] control_1_p5, registerfile_1_da, registerfile_1_da_2;
  wire [15:0] alu_1_rdata, control_1_p8, InstrReg_q, PC_out, ramdualport_1_d, registerfile_1_db;

  Counter Phase (.en(1'b1), .C(clk), .clr(1'b0), .out(InstrEx));  // open: ovf
  not not_1 (InstrL, InstrEx);
  CounterPreset #(.Bits(16)) PC (
    .en(in_4), .C(clk), .dir(in_5), .in(in_7), .ld(in_6), .clr(in_8), .out(PC_out), .ovf(PC_ovf));
  // Probe on PC_ovf
  RAMDualPort #(.AddrBits(16), .isProgramMemory("true"), .Bits(16)) ramdualport_1 (
    .A(PC_out), .Din(in_10), .str(in_9), .C(clk), .ld(1'b1), .D(ramdualport_1_d));
  Register #(.Bits(16)) InstrReg (.D(ramdualport_1_d), .C(clk), .en(InstrL), .Q(InstrReg_q));
  RegisterFile #(.AddrBits(4), .Bits(16)) registerfile_1 (
    .Din(control_1_p8), .we(RTW), .Rw(RT), .C(clk), .Ra(RT), .Rb(in_2),
    .Da({registerfile_1_da_2, registerfile_1_da}), .Db(registerfile_1_db));
  // Probe on InstrReg_q
  // control control_1: pin names not known; wires that end beside it: InstrReg_q, InstrEx, RT, RTW, control_1_p5, control_1_p6, control_1_p7, control_1_p8
  alu alu_1 (
    .Op(in_3), .TData({registerfile_1_da_2, registerfile_1_da}), .AData(registerfile_1_db),
    .RData(alu_1_rdata));
  // Probe on alu_1_rdata
  // Probe on control_1_p5
  assign control_1_p8 = control_1_p6 ? {registerfile_1_da_2, control_1_p5} : 16'bz;  // Driver driver_1
  assign control_1_p8 = control_1_p7 ? {control_1_p5, registerfile_1_da} : 16'bz;  // Driver driver_2
  // Probe on control_1_p8

  // Notes on the sheet:
  //   Imm
  //   Data
endmodule
